// Logisim project ComP.circ as structural Verilog: 4 circuits, main circuit main
module main (
  input  in_1,
  input  on_clk,
  input  Enable,
  input  [15:0] in_4,
  input  [7:0] in_5
);

  wire alu_1_bandeira, alu_1_igual, alu_1_maior, alu_1_menor, and_1_out, clock_1_out, or_1_out, undriven,
       undriven_2;
  wire [7:0] pc8_1_output, rom_2_data;
  wire [15:0] alu_1_dados, program_counter_1_output, register_1_q, register_2_q;

  Hex_Digit_Display hex_digit_display_1 (.value(alu_1_dados[11:8]), .dp(undriven));
  Hex_Digit_Display hex_digit_display_2 (.value(alu_1_dados[15:12]), .dp(undriven));
  Hex_Digit_Display hex_digit_display_3 (.value(alu_1_dados[3:0]), .dp(undriven));
  Hex_Digit_Display hex_digit_display_4 (.value(alu_1_dados[7:4]), .dp(undriven));
  ALU alu_1 (
    .A_ENTRADA(register_1_q), .B_ENTRADA(register_2_q), .SUB(rom_2_data[7]), .SOM(rom_2_data[6]),
    .AND_AB(rom_2_data[5]), .XOR_AB(rom_2_data[4]), .NAND_AB(rom_2_data[3]), .NOT_A(rom_2_data[2]),
    .NOR_AB(rom_2_data[1]), .OR_AB(rom_2_data[0]), .MAIOR(alu_1_maior), .IGUAL(alu_1_igual),
    .MENOR(alu_1_menor), .DADOS(alu_1_dados), .BANDEIRA(alu_1_bandeira));  // open: ENTRADA_C_SB, SAIDA_C_SB, ENTRADA_C_SO, SAIDA_C_SO
  Register #(.width(16)) register_1 (.D(alu_1_dados), .en(Enable), .Q(register_1_q), .clk(and_1_out));  // open: clr
  Register #(.width(16)) register_2 (.D(alu_1_dados), .en(Enable), .Q(register_2_q), .clk(and_1_out));  // open: clr
  RAM #(.addrWidth(16), .dataWidth(16)) ram_1 (
    .addr(program_counter_1_output), .data(alu_1_dados), .sel(undriven_2), .clk(on_clk), .ld(on_clk),
    .clr(or_1_out));
  Program_Counter program_counter_1 (.Reset(or_1_out), .in_1(in_4), .Clk(and_1_out), .Output(program_counter_1_output));
  or or_1 (or_1_out, alu_1_bandeira, in_1);
  and and_1 (and_1_out, on_clk, clock_1_out);
  Clock clock_1 (.out(clock_1_out));
  PC8 pc8_1 (.Reset(or_1_out), .in_1(in_5), .Clk(and_1_out), .Output(pc8_1_output));
  ROM #(.addrWidth(16), .dataWidth(16)) rom_1 (.addr(program_counter_1_output), .data(alu_1_dados), .sel(undriven_2));
  ROM rom_2 (.addr(pc8_1_output), .data(rom_2_data), .sel(undriven_2));

  // Notes on the sheet:
  //   contents of rom_1 (hex, n*v repeats v):
  //   101 1001 1001 11
  //   contents of rom_2 (hex, n*v repeats v):
  //   4*8
endmodule

module ALU (
  input  [15:0] A_ENTRADA,
  input  [15:0] B_ENTRADA,
  input  ENTRADA_C_SB,
  input  SAIDA_C_SB,
  input  SUB,
  input  ENTRADA_C_SO,
  input  SAIDA_C_SO,
  input  SOM,
  input  AND_AB,
  input  XOR_AB,
  input  NAND_AB,
  input  NOT_A,
  input  NOR_AB,
  input  OR_AB,
  output MAIOR,
  output IGUAL,
  output MENOR,
  output [15:0] DADOS,
  output BANDEIRA
);

  wire and_2_out, and_3_out, and_4_out, and_5_out, and_6_out, and_7_out, and_8_out, and_9_out, and_10_out,
       and_11_out, and_12_out, and_13_out, and_14_out, and_15_out, and_16_out, not_2_out, not_3_out,
       not_4_out, not_5_out, not_6_out, not_7_out, not_8_out, not_9_out, not_10_out, not_11_out, not_12_out,
       not_13_out, not_14_out, not_15_out, not_16_out, not_17_out;
  wire [15:0] adder_1_out, and_1_out, nand_1_out, nor_1_out, not_1_out, or_1_out, or_2_out, subtractor_1_out,
       xor_1_out;

  Comparator #(.width(16)) comparator_1 (.a(A_ENTRADA), .b(B_ENTRADA), .gt(MAIOR), .eq(IGUAL), .lt(MENOR));
  Subtractor #(.width(16)) subtractor_1 (
    .a(A_ENTRADA), .b(B_ENTRADA), .out(subtractor_1_out), .bin(ENTRADA_C_SB), .bout(SAIDA_C_SB));
  Adder #(.width(16)) adder_1 (.a(A_ENTRADA), .b(B_ENTRADA), .out(adder_1_out), .cin(ENTRADA_C_SO), .cout(SAIDA_C_SO));
  assign and_1_out = A_ENTRADA & B_ENTRADA;  // AND_Gate and_1, 16 bits wide
  assign xor_1_out = A_ENTRADA ^ B_ENTRADA;  // XOR_Gate xor_1, 16 bits wide
  assign nand_1_out = ~(A_ENTRADA & B_ENTRADA);  // NAND_Gate nand_1, 16 bits wide
  assign not_1_out = ~A_ENTRADA;  // NOT_Gate not_1, 16 bits wide
  assign nor_1_out = ~(A_ENTRADA | B_ENTRADA);  // NOR_Gate nor_1, 16 bits wide
  assign or_1_out = A_ENTRADA | B_ENTRADA;  // OR_Gate or_1, 16 bits wide
  assign DADOS = SUB ? subtractor_1_out : 16'bz;  // Controlled_Buffer controlled_buffer_1
  assign DADOS = SOM ? adder_1_out : 16'bz;  // Controlled_Buffer controlled_buffer_2
  assign DADOS = AND_AB ? and_1_out : 16'bz;  // Controlled_Buffer controlled_buffer_3
  assign DADOS = XOR_AB ? xor_1_out : 16'bz;  // Controlled_Buffer controlled_buffer_4
  assign DADOS = NAND_AB ? nand_1_out : 16'bz;  // Controlled_Buffer controlled_buffer_5
  assign DADOS = NOT_A ? not_1_out : 16'bz;  // Controlled_Buffer controlled_buffer_6
  assign DADOS = NOR_AB ? nor_1_out : 16'bz;  // Controlled_Buffer controlled_buffer_7
  assign DADOS = OR_AB ? or_1_out : 16'bz;  // Controlled_Buffer controlled_buffer_8
  assign or_2_out = DADOS;  // OR_Gate or_2, 16 bits wide OR_Gate
  not not_2 (not_2_out, or_2_out[3]);
  not not_3 (not_3_out, or_2_out[0]);
  not not_4 (not_4_out, or_2_out[2]);
  not not_5 (not_5_out, or_2_out[1]);
  and and_2 (and_2_out, not_3_out, not_5_out);
  and and_3 (and_3_out, and_2_out, not_4_out);
  and and_4 (and_4_out, and_3_out, not_2_out);
  and and_5 (and_5_out, and_4_out, not_8_out);
  not not_6 (not_6_out, or_2_out[5]);
  not not_7 (not_7_out, or_2_out[6]);
  not not_8 (not_8_out, or_2_out[4]);
  not not_9 (not_9_out, or_2_out[7]);
  and and_6 (and_6_out, and_5_out, not_6_out);
  and and_7 (and_7_out, and_6_out, not_7_out);
  and and_8 (and_8_out, and_7_out, not_9_out);
  not not_10 (not_10_out, or_2_out[10]);
  not not_11 (not_11_out, or_2_out[9]);
  not not_12 (not_12_out, or_2_out[11]);
  not not_13 (not_13_out, or_2_out[8]);
  and and_9 (and_9_out, and_8_out, not_13_out);
  and and_10 (and_10_out, and_9_out, not_11_out);
  and and_11 (and_11_out, and_10_out, not_10_out);
  and and_12 (and_12_out, and_11_out, not_12_out);
  not not_14 (not_14_out, or_2_out[14]);
  not not_15 (not_15_out, or_2_out[12]);
  not not_16 (not_16_out, or_2_out[13]);
  not not_17 (not_17_out, or_2_out[15]);
  and and_13 (and_13_out, and_12_out, not_15_out);
  buf and_14 (and_14_out, and_13_out);  // AND_Gate
  and and_15 (and_15_out, and_14_out, not_16_out);
  and and_16 (and_16_out, and_15_out, not_14_out);
  and and_17 (BANDEIRA, and_16_out, not_17_out);
  Pull_Resistor pull_resistor_1 (.node(or_2_out[0]));
  Pull_Resistor pull_resistor_2 (.node(or_2_out[1]));
  Pull_Resistor pull_resistor_3 (.node(or_2_out[2]));
  Pull_Resistor pull_resistor_4 (.node(or_2_out[3]));
  Pull_Resistor pull_resistor_5 (.node(or_2_out[4]));
  Pull_Resistor pull_resistor_6 (.node(or_2_out[5]));
  Pull_Resistor pull_resistor_7 (.node(or_2_out[6]));
  Pull_Resistor pull_resistor_8 (.node(or_2_out[7]));
  Pull_Resistor pull_resistor_9 (.node(or_2_out[8]));
  Pull_Resistor pull_resistor_10 (.node(or_2_out[9]));
  Pull_Resistor pull_resistor_11 (.node(or_2_out[10]));
  Pull_Resistor pull_resistor_12 (.node(or_2_out[11]));
  Pull_Resistor pull_resistor_13 (.node(or_2_out[12]));
  Pull_Resistor pull_resistor_14 (.node(or_2_out[13]));
  Pull_Resistor pull_resistor_15 (.node(or_2_out[14]));
  Pull_Resistor pull_resistor_16 (.node(or_2_out[15]));
endmodule

module Program_Counter (
  input  [15:0] in_1,
  input  Reset,
  input  Clk,
  output [15:0] Output
);

  wire [15:0] adder_1_out;

  Adder #(.width(16)) adder_1 (.a(Output), .b(in_1), .out(adder_1_out));  // open: cin, cout
  Register #(.width(16)) register_1 (.D(adder_1_out), .Q(Output), .clk(Clk), .clr(Reset));  // open: en
endmodule

module PC8 (
  input  [7:0] in_1,
  input  Reset,
  input  Clk,
  output [7:0] Output
);

  wire [7:0] adder_1_out;

  Adder adder_1 (.a(Output), .b(in_1), .out(adder_1_out));  // open: cin, cout
  Register register_1 (.D(adder_1_out), .Q(Output), .clk(Clk), .clr(Reset));  // open: en
  // also tied to GND on the sheet: {in_1[1], in_1[2], in_1[3], in_1[4], in_1[5], in_1[6], in_1[7]}
  // also tied to VCC on the sheet: in_1[0]
endmodule
