// Logisim project 4Bit adder.circ as structural Verilog: 1 circuit, main circuit main
module main (
  input  Carry,
  input  A0,
  input  B0,
  input  A1,
  input  B1,
  input  A2,
  input  B2,
  input  A3,
  input  B3,
  output S0,
  output S1,
  output S2,
  output S3,
  output SC
);

  wire main_1_p4, main_2_sum, main_3_p4;

  // Adder_main main_1: pin names not known; wires that end beside it: A0, B0, Carry, main_1_p4, S0
  Adder_main main_2 (.A(A1), .B(B1), .C(main_1_p4), .Carry(S1), .Sum(main_2_sum));
  // Adder_main main_3: pin names not known; wires that end beside it: A2, B2, main_2_sum, main_3_p4, S2
  // Adder_main main_4: pin names not known; wires that end beside it: A3, B3, main_3_p4, SC, S3
endmodule
