// Logisim project ALU.circ as structural Verilog: 1 circuit, main circuit main
// ALU
module main (
  input  ENTRADA_SUB,
  input  ENTRADA_ADD,
  input  [15:0] A_IN,
  input  [15:0] B_IN,
  input  ADD,
  input  SUB,
  input  MULT,
  input  DIV,
  input  NOT_A,
  input  A_AND_B,
  input  A_XOR_B,
  input  A_OR_B,
  input  A_NOR_B,
  input  A_NAND_B,
  output MAIOR,
  output IGUAL,
  output MENOR,
  output SOBRA_ADD,
  output SOBRA_SUB,
  output [15:0] SOBRA_MULT,
  output [15:0] SOBRA_DIV,
  output [15:0] DADOS
);

  wire [15:0] adder_1_out, and_1_out, divider_1_out, multiplier_1_out, nand_1_out, nor_1_out, not_1_out,
       or_1_out, or_2_out, subtractor_1_out, xor_1_out;

  assign not_1_out = ~A_IN;  // NOT_Gate not_1, 16 bits wide
  assign and_1_out = A_IN & B_IN;  // AND_Gate and_1, 16 bits wide
  assign or_1_out = A_IN | B_IN;  // OR_Gate or_1, 16 bits wide
  Comparator #(.width(16)) comparator_1 (.a(A_IN), .b(B_IN), .gt(MAIOR), .eq(IGUAL), .lt(MENOR));
  Adder #(.width(16)) adder_1 (.a(A_IN), .b(A_IN), .out(adder_1_out), .cin(ENTRADA_ADD), .cout(SOBRA_ADD));
  Subtractor #(.width(16)) subtractor_1 (
    .a(A_IN), .b(B_IN), .out(subtractor_1_out), .bin(ENTRADA_SUB), .bout(SOBRA_SUB));
  Multiplier #(.width(16)) multiplier_1 (.a(A_IN), .b(B_IN), .out(multiplier_1_out), .cout(SOBRA_MULT));  // open: cin
  Divider #(.width(16)) divider_1 (.a(A_IN), .b(B_IN), .out(divider_1_out), .rem(SOBRA_DIV));  // open: upper
  assign xor_1_out = A_IN ^ B_IN;  // XOR_Gate xor_1, 16 bits wide
  assign nor_1_out = ~(A_IN | B_IN);  // NOR_Gate nor_1, 16 bits wide
  assign nand_1_out = ~(A_IN & B_IN);  // NAND_Gate nand_1, 16 bits wide
  assign DADOS = ADD ? adder_1_out : 16'bz;  // Controlled_Buffer controlled_buffer_1
  assign DADOS = SUB ? subtractor_1_out : 16'bz;  // Controlled_Buffer controlled_buffer_2
  assign DADOS = MULT ? multiplier_1_out : 16'bz;  // Controlled_Buffer controlled_buffer_3
  assign DADOS = DIV ? divider_1_out : 16'bz;  // Controlled_Buffer controlled_buffer_4
  assign DADOS = NOT_A ? not_1_out : 16'bz;  // Controlled_Buffer controlled_buffer_5
  assign DADOS = A_AND_B ? and_1_out : 16'bz;  // Controlled_Buffer controlled_buffer_6
  assign DADOS = A_XOR_B ? xor_1_out : 16'bz;  // Controlled_Buffer controlled_buffer_7
  assign DADOS = A_OR_B ? or_1_out : 16'bz;  // Controlled_Buffer controlled_buffer_8
  assign DADOS = A_NOR_B ? nor_1_out : 16'bz;  // Controlled_Buffer controlled_buffer_9
  assign DADOS = A_NAND_B ? nand_1_out : 16'bz;  // Controlled_Buffer controlled_buffer_10
  assign or_2_out = DADOS;  // OR_Gate or_2, 16 bits wide OR_Gate
  Pull_Resistor pull_resistor_1 (.node(or_2_out[0]));
  Pull_Resistor pull_resistor_2 (.node(or_2_out[1]));
  Pull_Resistor pull_resistor_3 (.node(or_2_out[2]));
  Pull_Resistor pull_resistor_4 (.node(or_2_out[3]));
  Pull_Resistor pull_resistor_5 (.node(or_2_out[4]));
  Pull_Resistor pull_resistor_6 (.node(or_2_out[5]));
  Pull_Resistor pull_resistor_7 (.node(or_2_out[6]));
  Pull_Resistor pull_resistor_8 (.node(or_2_out[7]));
  Pull_Resistor pull_resistor_9 (.node(or_2_out[8]));
  Pull_Resistor pull_resistor_10 (.node(or_2_out[9]));
  Pull_Resistor pull_resistor_11 (.node(or_2_out[10]));
  Pull_Resistor pull_resistor_12 (.node(or_2_out[11]));
  Pull_Resistor pull_resistor_13 (.node(or_2_out[12]));
  Pull_Resistor pull_resistor_14 (.node(or_2_out[13]));
  Pull_Resistor pull_resistor_15 (.node(or_2_out[14]));
  Pull_Resistor pull_resistor_16 (.node(or_2_out[15]));
endmodule
