// Logisim project Adder.circ as structural Verilog: 1 circuit, main circuit main
module main (
  input  A,
  input  B,
  input  C,
  output Carry,
  output Sum
);

  wire and_1_out, and_2_out, xor_1_out;

  and and_1 (and_1_out, A, B);
  xor xor_1 (xor_1_out, A, B);
  and and_2 (and_2_out, xor_1_out, C);
  xor xor_2 (Sum, xor_1_out, C);
  or or_1 (Carry, and_1_out, and_2_out);
endmodule
