// Logisim project codificador.circ as structural Verilog: 1 circuit, main circuit main
module main (
  input  E0,
  input  E1,
  input  E2,
  input  E3,
  input  E4,
  input  E5,
  input  E6,
  input  E7,
  input  E8,
  input  E9,
  output SA,
  output SB,
  output SC,
  output SD
);

  or or_1 (SA, E9, E8);
  or or_2 (SB, E7, E6, E5, E4);
  or or_3 (SC, E7, E6, E3, E2);
  or or_4 (SD, E9, E7, E5, E3, E1);
endmodule
