// Logisim project memoria.circ as structural Verilog: 1 circuit, main circuit main
module main (
  input  E0,
  input  E1,
  input  E2,
  input  E3,
  input  E4,
  input  E5,
  input  E6,
  input  E7,
  input  E8,
  input  CL,
  input  ENT,
  output S0,
  output S,
  output S2,
  output S3,
  output S4,
  output S5,
  output S6,
  output S7,
  output S8
);

  wire buffer_1_out, or_1_out, or_2_out, or_3_out, or_4_out, or_5_out, or_6_out, or_7_out, or_8_out, or_9_out;

  or or_1 (or_1_out, E0, CL);
  or or_2 (or_2_out, E1, CL);
  or or_3 (or_3_out, E2, CL);
  or or_4 (or_4_out, E3, CL);
  or or_5 (or_5_out, E4, CL);
  or or_6 (or_6_out, E5, CL);
  or or_7 (or_7_out, E6, CL);
  or or_8 (or_8_out, E7, CL);
  or or_9 (or_9_out, E8, CL);
  buf buffer_1 (buffer_1_out, CL);
  J_K_Flip_Flop j_k_ff_1 (.J(ENT), .clk(or_1_out), .K(buffer_1_out), .Q(S0));  // open: Qn, preset, en, reset
  J_K_Flip_Flop j_k_ff_2 (.J(ENT), .clk(or_2_out), .K(buffer_1_out), .Q(S));  // open: Qn, preset, en, reset
  J_K_Flip_Flop j_k_ff_3 (.J(ENT), .clk(or_3_out), .K(buffer_1_out), .Q(S2));  // open: Qn, preset, en, reset
  J_K_Flip_Flop j_k_ff_4 (.J(ENT), .clk(or_4_out), .K(buffer_1_out), .Q(S3));  // open: Qn, preset, en, reset
  J_K_Flip_Flop j_k_ff_5 (.J(ENT), .clk(or_5_out), .K(buffer_1_out), .Q(S4));  // open: Qn, preset, en, reset
  J_K_Flip_Flop j_k_ff_6 (.J(ENT), .clk(or_6_out), .K(buffer_1_out), .Q(S5));  // open: Qn, preset, en, reset
  J_K_Flip_Flop j_k_ff_7 (.J(ENT), .clk(or_7_out), .K(buffer_1_out), .Q(S6));  // open: Qn, preset, en, reset
  J_K_Flip_Flop j_k_ff_8 (.J(ENT), .clk(or_8_out), .K(buffer_1_out), .Q(S7));  // open: Qn, preset, en, reset
  J_K_Flip_Flop j_k_ff_9 (.J(ENT), .clk(or_9_out), .K(buffer_1_out), .Q(S8));  // open: Qn, preset, en, reset
endmodule
