// Logisim project pj.circ as structural Verilog: 1 circuit, main circuit main
module main (
);

  wire main_1_sa, main_1_sb, main_2_sd, main_3_s0, main_3_s1, main_3_s2, main_3_s3, main_4_p5, main_4_p6,
       main_4_p7, main_4_p8, main_4_p9, main_4_p10, main_4_p11;

  codificador_main main_1 (.SA(main_1_sa), .SB(main_1_sb));  // open: E0, E1, E2, E3, E4, E5, E6, E7, E8, E9, SC, SD
  codificador_main main_2 (.SD(main_2_sd));  // open: E0, E1, E2, E3, E4, E5, E6, E7, E8, E9, SA, SB, SC
  _4Bit_adder_main main_3 (
    .Carry(main_1_sa), .A0(main_2_sd), .B0(main_1_sb), .S0(main_3_s0), .S1(main_3_s1), .S2(main_3_s2),
    .S3(main_3_s3));  // open: A1, B1, A2, B2, A3, B3, SC
  // descodificador_main main_4: pin names not known; wires that end beside it: main_3_s0, main_3_s1, main_3_s2, main_3_s3, main_4_p5, main_4_p6, main_4_p7, main_4_p8, main_4_p9, main_4_p10, main_4_p11
  _7_Segment_Display u_7_segment_display_1 (
    .g(main_4_p11), .f(main_4_p10), .a(main_4_p5), .b(main_4_p6), .e(main_4_p9), .d(main_4_p8), .c(main_4_p7));  // open: dp
endmodule
