// Logisim project pj1.circ as structural Verilog: 1 circuit, main circuit main
module main (
  input  in_1,
  input  SUB,
  input  in_3,
  input  in_4,
  input  in_5,
  input  in_6,
  input  in_7,
  input  in_8,
  input  in_9,
  input  in_10,
  input  in_11,
  input  in_12,
  input  in_13,
  output out_14
);

  wire demultiplexer_1_out0, demultiplexer_1_out1, demultiplexer_2_out0, demultiplexer_2_out1,
       demultiplexer_3_out0, demultiplexer_3_out1, demultiplexer_4_out0, demultiplexer_4_out1,
       demultiplexer_5_out0, demultiplexer_5_out1, demultiplexer_6_out0, demultiplexer_6_out1,
       demultiplexer_7_out0, demultiplexer_7_out1, demultiplexer_8_out0, demultiplexer_8_out1,
       demultiplexer_9_out0, demultiplexer_9_out1, main_1_s, main_1_s0, main_1_s2, main_1_s3, main_1_s4,
       main_1_s5, main_1_s6, main_1_s7, main_1_s8, main_2_s, main_2_s0, main_2_s2, main_2_s3, main_2_s4,
       main_2_s5, main_2_s6, main_2_s7, main_2_s8, main_3_sa, main_3_sb, main_3_sc, main_3_sd, main_4_sa,
       main_4_sb, main_4_sc, main_4_sd, main_5_s0, main_5_s1, main_5_s2, main_5_s3, main_6_a, main_6_b,
       main_6_c, main_6_d, main_6_e, main_6_f, main_6_g, undriven, undriven_2, xor_1_out, xor_2_out,
       xor_3_out, xor_4_out;

  Demultiplexer demultiplexer_1 (
    .out0(demultiplexer_1_out0), .out1(demultiplexer_1_out1), .in(in_1), .sel(undriven_2), .en(undriven));
  Demultiplexer demultiplexer_2 (
    .out0(demultiplexer_2_out0), .out1(demultiplexer_2_out1), .in(in_3), .sel(undriven_2), .en(undriven));
  Demultiplexer demultiplexer_3 (
    .out0(demultiplexer_3_out0), .out1(demultiplexer_3_out1), .in(in_4), .sel(undriven_2), .en(undriven));
  Demultiplexer demultiplexer_4 (
    .out0(demultiplexer_4_out0), .out1(demultiplexer_4_out1), .in(in_5), .sel(undriven_2), .en(undriven));
  Demultiplexer demultiplexer_5 (
    .out0(demultiplexer_5_out0), .out1(demultiplexer_5_out1), .in(in_6), .sel(undriven_2), .en(undriven));
  Demultiplexer demultiplexer_6 (
    .out0(demultiplexer_6_out0), .out1(demultiplexer_6_out1), .in(in_7), .sel(undriven_2), .en(undriven));
  Demultiplexer demultiplexer_7 (
    .out0(demultiplexer_7_out0), .out1(demultiplexer_7_out1), .in(in_8), .sel(undriven_2), .en(undriven));
  Demultiplexer demultiplexer_8 (
    .out0(demultiplexer_8_out0), .out1(demultiplexer_8_out1), .in(in_9), .sel(undriven_2), .en(undriven));
  Demultiplexer demultiplexer_9 (
    .out0(demultiplexer_9_out0), .out1(demultiplexer_9_out1), .in(in_10), .sel(undriven_2), .en(undriven));
  Register register_1 (.clk(in_13), .clr(undriven_2));  // open: D, en, Q
  memoria_main main_1 (
    .E0(demultiplexer_1_out0), .E1(demultiplexer_2_out0), .E2(demultiplexer_3_out0),
    .E3(demultiplexer_4_out0), .E4(demultiplexer_5_out0), .E5(demultiplexer_6_out0),
    .E6(demultiplexer_7_out0), .E7(demultiplexer_8_out0), .E8(demultiplexer_9_out0), .CL(in_11), .ENT(in_12),
    .S0(main_1_s0), .S(main_1_s), .S2(main_1_s2), .S3(main_1_s3), .S4(main_1_s4), .S5(main_1_s5),
    .S6(main_1_s6), .S7(main_1_s7), .S8(main_1_s8));
  memoria_main main_2 (
    .E0(demultiplexer_1_out1), .E1(demultiplexer_2_out1), .E2(demultiplexer_3_out1),
    .E3(demultiplexer_4_out1), .E4(demultiplexer_5_out1), .E5(demultiplexer_6_out1),
    .E6(demultiplexer_7_out1), .E7(demultiplexer_8_out1), .E8(demultiplexer_9_out1), .CL(in_11), .ENT(in_12),
    .S0(main_2_s0), .S(main_2_s), .S2(main_2_s2), .S3(main_2_s3), .S4(main_2_s4), .S5(main_2_s5),
    .S6(main_2_s6), .S7(main_2_s7), .S8(main_2_s8));
  codificador_main main_3 (
    .E1(main_1_s0), .E2(main_1_s), .E3(main_1_s2), .E4(main_1_s3), .E5(main_1_s4), .E6(main_1_s5),
    .E7(main_1_s6), .E8(main_1_s7), .E9(main_1_s8), .SA(main_3_sa), .SB(main_3_sb), .SC(main_3_sc),
    .SD(main_3_sd));  // open: E0
  codificador_main main_4 (
    .E1(main_2_s0), .E2(main_2_s), .E3(main_2_s2), .E4(main_2_s3), .E5(main_2_s4), .E6(main_2_s5),
    .E7(main_2_s6), .E8(main_2_s7), .E9(main_2_s8), .SA(main_4_sa), .SB(main_4_sb), .SC(main_4_sc),
    .SD(main_4_sd));  // open: E0
  xor xor_1 (xor_1_out, SUB, main_3_sa);
  xor xor_2 (xor_2_out, SUB, main_3_sb);
  xor xor_3 (xor_3_out, SUB, main_3_sc);
  xor xor_4 (xor_4_out, SUB, main_3_sd);
  _4Bit_adder_main main_5 (
    .Carry(SUB), .A0(xor_4_out), .B0(main_4_sd), .A1(xor_3_out), .B1(main_4_sc), .A2(xor_2_out),
    .B2(main_4_sb), .A3(xor_1_out), .B3(main_4_sa), .S0(main_5_s0), .S1(main_5_s1), .S2(main_5_s2),
    .S3(main_5_s3), .SC(out_14));
  decodificador_main main_6 (
    .A0(main_5_s3), .A1(main_5_s2), .A2(main_5_s1), .A3(main_5_s0), .a(main_6_a), .b(main_6_b), .c(main_6_c),
    .d(main_6_d), .e(main_6_e), .f(main_6_f), .g(main_6_g));
  _7_Segment_Display u_7_segment_display_1 (
    .g(main_6_g), .f(main_6_f), .a(main_6_a), .b(main_6_b), .e(main_6_e), .d(main_6_d), .c(main_6_c));  // open: dp
endmodule
