// Logisim project shift r.circ as structural Verilog: 1 circuit, main circuit main
module main (
  input  clk,
  input  entrada,
  output s1,
  output s2,
  output s3,
  output s4,
  output s5,
  output s6,
  output s7,
  output s8,
  output s9,
  output s10,
  output s11,
  output s12,
  output s13,
  output s14,
  output s15,
  output s16
);

  D_Flip_Flop d_ff_1 (.clk(clk), .D(entrada), .Q(s1));  // open: Qn, preset, en, reset
  D_Flip_Flop d_ff_2 (.clk(clk), .D(s8), .Q(s9));  // open: Qn, preset, en, reset
  D_Flip_Flop d_ff_3 (.clk(clk), .D(s1), .Q(s2));  // open: Qn, preset, en, reset
  D_Flip_Flop d_ff_4 (.clk(clk), .D(s9), .Q(s10));  // open: Qn, preset, en, reset
  D_Flip_Flop d_ff_5 (.clk(clk), .D(s2), .Q(s3));  // open: Qn, preset, en, reset
  D_Flip_Flop d_ff_6 (.clk(clk), .D(s10), .Q(s11));  // open: Qn, preset, en, reset
  D_Flip_Flop d_ff_7 (.clk(clk), .D(s3), .Q(s4));  // open: Qn, preset, en, reset
  D_Flip_Flop d_ff_8 (.clk(clk), .D(s11), .Q(s12));  // open: Qn, preset, en, reset
  D_Flip_Flop d_ff_9 (.clk(clk), .D(s4), .Q(s5));  // open: Qn, preset, en, reset
  D_Flip_Flop d_ff_10 (.clk(clk), .D(s12), .Q(s13));  // open: Qn, preset, en, reset
  D_Flip_Flop d_ff_11 (.clk(clk), .D(s5), .Q(s6));  // open: Qn, preset, en, reset
  D_Flip_Flop d_ff_12 (.clk(clk), .D(s13), .Q(s14));  // open: Qn, preset, en, reset
  D_Flip_Flop d_ff_13 (.clk(clk), .D(s6), .Q(s7));  // open: Qn, preset, en, reset
  D_Flip_Flop d_ff_14 (.clk(clk), .D(s14), .Q(s15));  // open: Qn, preset, en, reset
  D_Flip_Flop d_ff_15 (.clk(clk), .D(s7), .Q(s8));  // open: Qn, preset, en, reset
  D_Flip_Flop d_ff_16 (.clk(clk), .D(s15), .Q(s16));  // open: Qn, preset, en, reset
endmodule
